# Fritzing sketch ISL29125.fz (saved by Fritzing 0.9.3b)
circuit board: 5.43663cm x 2.53528cm
breadboards: 1

parts:
  U2 = SIP - 5 pins [chip_label=29125 package="SIP (Single Inline) [THT]"]
  Raspberry_Pi_3B+ = Raspberry Pi B+

nets:
  GND: U2.GND, Raspberry_Pi_3B+.GND
  3.3V: U2.3.3V, Raspberry_Pi_3B+.3v3
  N1: U2.SDA, Raspberry_Pi_3B+.GPIO2
  N2: U2.SCl, Raspberry_Pi_3B+.GPIO3

notes:
  GND
  3.3V
  SDA
  SCL
  Denald Demirxhiu

custom parts:
  SIP - 5 pins: A SIP stand-in part for whatever you want. With 5 pins on a 300 mil single inline package (SIP) footprint.
